// Logisim project проект.circ as structural Verilog: 5 circuits, main circuit main
module main (
  input  Game_Over
);

  wire and_1_out, and_2_out, clock_1_out, clock_2_out, comparator_1_eq, counter_2_carry, counter_3_carry,
       counter_4_carry, jump_out;
  wire [3:0] count1, count2, count3, count4;
  wire [4:0] counter_1_q;
  wire [31:0] D1, D2, D3, D4, D5, D6, D7, D8, D9, dino_1_out_11, dino_1_out_12, dino_1_out_13, dino_1_out_14,
       dino_1_out_15, dino_1_out_16, dino_1_out_17, dino_1_out_18, dino_1_out_19, dino_1_out_20,
       dino_1_out_21, dino_1_out_22, dino_1_out_23, dino_1_out_24, dino_1_out_25, dino_1_out_26,
       dino_1_out_27, dino_1_out_28, dino_1_out_29, dino_1_out_30, dino_1_out_31, dino_1_out_32,
       dino_1_out_33, dino_1_out_34, dino_1_out_35, dino_1_out_36, dino_1_out_37, dino_1_out_38,
       dino_1_out_39, dino_1_out_40, dino_1_out_41, dino_1_out_42;

  Clock clock_1 (.out(clock_1_out));
  Hex_Digit_Display hex_digit_display_1 (.value(count2));  // open: dp
  Hex_Digit_Display hex_digit_display_2 (.value(count1));  // open: dp
  Counter #(.width(5), .max('h1f)) counter_1 (.Q(counter_1_q), .clk(clock_1_out));  // open: load, D, count, carry, clr
  Hex_Digit_Display hex_digit_display_3 (.value(count3));  // open: dp
  Comparator #(.width(5)) comparator_1 (.a(counter_1_q), .b({5{1'b1}}), .eq(comparator_1_eq));  // open: gt, lt
  Hex_Digit_Display hex_digit_display_4 (.value(count4));  // open: dp
  DotMatrix #(.matrixcols(32), .matrixrows(32)) dotmatrix_1 (
    .col0(dino_1_out_11), .col1(dino_1_out_12), .col2(dino_1_out_13), .col3(dino_1_out_14),
    .col4(dino_1_out_15), .col5(dino_1_out_16), .col6(dino_1_out_17), .col7(dino_1_out_18),
    .col8(dino_1_out_19), .col9(dino_1_out_20), .col10(dino_1_out_21), .col11(dino_1_out_22),
    .col12(dino_1_out_23), .col13(dino_1_out_24), .col14(dino_1_out_25), .col15(dino_1_out_26),
    .col16(dino_1_out_27), .col17(dino_1_out_28), .col18(dino_1_out_29), .col19(dino_1_out_30),
    .col20(dino_1_out_31), .col21(dino_1_out_32), .col22(dino_1_out_33), .col23(dino_1_out_34),
    .col24(dino_1_out_35), .col25(dino_1_out_36), .col26(dino_1_out_37), .col27(dino_1_out_38),
    .col28(dino_1_out_39), .col29(dino_1_out_40), .col30(dino_1_out_41), .col31(dino_1_out_42));
  dino dino_1 (
    .stop(Game_Over), .out_11(dino_1_out_11), .out_12(dino_1_out_12), .out_13(dino_1_out_13),
    .out_14(dino_1_out_14), .out_15(dino_1_out_15), .out_16(dino_1_out_16), .out_17(dino_1_out_17),
    .out_18(dino_1_out_18), .out_19(dino_1_out_19), .out_20(dino_1_out_20), .out_21(dino_1_out_21),
    .out_22(dino_1_out_22), .out_23(dino_1_out_23), .out_24(dino_1_out_24), .out_25(dino_1_out_25),
    .out_26(dino_1_out_26), .out_27(dino_1_out_27), .out_28(dino_1_out_28), .out_29(dino_1_out_29),
    .out_30(dino_1_out_30), .out_31(dino_1_out_31), .out_32(dino_1_out_32), .out_33(dino_1_out_33),
    .out_34(dino_1_out_34), .out_35(dino_1_out_35), .out_36(dino_1_out_36), .out_37(dino_1_out_37),
    .out_38(dino_1_out_38), .out_39(dino_1_out_39), .out_40(dino_1_out_40), .out_41(dino_1_out_41),
    .out_42(dino_1_out_42), .in_2(D1), .in_3(D2), .in_4(D3), .in_5(D4), .in_6(D5), .in_7(D6), .in_8(D7),
    .in_9(D8), .in_10(D9));
  Counter #(.width(4), .max('h9)) counter_2 (
    .Q(count4), .carry(counter_2_carry), .clk(comparator_1_eq));  // open: load, D, count, clr
  Counter #(.width(4), .max('h9)) counter_3 (
    .count(counter_2_carry), .Q(count3), .carry(counter_3_carry), .clk(comparator_1_eq));  // open: load, D, clr
  Counter #(.width(4), .max('h9)) counter_4 (
    .count(and_1_out), .Q(count2), .carry(counter_4_carry), .clk(comparator_1_eq));  // open: load, D, clr
  and and_1 (and_1_out, counter_3_carry, counter_2_carry);
  Counter #(.width(4), .max('h9)) counter_5 (
    .count(and_2_out), .Q(count1), .clk(comparator_1_eq));  // open: load, D, carry, clr
  and and_2 (and_2_out, counter_4_carry, and_1_out);
  Clock clock_2 (.out(clock_2_out));
  Button jump (.out(jump_out));
  jump jump_2 (
    .clock(clock_2_out), .jump(jump_out), .out_3(D1), .out_4(D2), .out_5(D3), .out_6(D4), .out_7(D5),
    .out_8(D6), .out_9(D7), .out_10(D8), .out_11(D9));
endmodule

module dino (
  input  stop,
  input  [31:0] in_2,
  input  [31:0] in_3,
  input  [31:0] in_4,
  input  [31:0] in_5,
  input  [31:0] in_6,
  input  [31:0] in_7,
  input  [31:0] in_8,
  input  [31:0] in_9,
  input  [31:0] in_10,
  output [31:0] out_11,
  output [31:0] out_12,
  output [31:0] out_13,
  output [31:0] out_14,
  output [31:0] out_15,
  output [31:0] out_16,
  output [31:0] out_17,
  output [31:0] out_18,
  output [31:0] out_19,
  output [31:0] out_20,
  output [31:0] out_21,
  output [31:0] out_22,
  output [31:0] out_23,
  output [31:0] out_24,
  output [31:0] out_25,
  output [31:0] out_26,
  output [31:0] out_27,
  output [31:0] out_28,
  output [31:0] out_29,
  output [31:0] out_30,
  output [31:0] out_31,
  output [31:0] out_32,
  output [31:0] out_33,
  output [31:0] out_34,
  output [31:0] out_35,
  output [31:0] out_36,
  output [31:0] out_37,
  output [31:0] out_38,
  output [31:0] out_39,
  output [31:0] out_40,
  output [31:0] out_41,
  output [31:0] out_42
);

  Multiplexer #(.width(32)) multiplexer_1 (.in0({32{1'b0}}), .in1({32{1'b0}}), .out(out_11), .sel(stop));  // open: en
  Multiplexer #(.width(32)) multiplexer_2 (.in0(in_2), .in1({32{1'b0}}), .out(out_12), .sel(stop));  // open: en
  Multiplexer #(.width(32)) multiplexer_3 (.in0(in_3), .in1({32{1'b0}}), .out(out_13), .sel(stop));  // open: en
  Multiplexer #(.width(32)) multiplexer_4 (.in0(in_4), .in1({32{1'b0}}), .out(out_14), .sel(stop));  // open: en
  Multiplexer #(.width(32)) multiplexer_5 (.in0(in_5), .in1({32{1'b0}}), .out(out_15), .sel(stop));  // open: en
  Multiplexer #(.width(32)) multiplexer_6 (.in0(in_6), .in1(32'h1fc00), .out(out_16), .sel(stop));  // open: en
  Multiplexer #(.width(32)) multiplexer_7 (.in0(in_7), .in1(32'h10400), .out(out_17), .sel(stop));  // open: en
  Multiplexer #(.width(32)) multiplexer_8 (.in0(in_8), .in1(32'h124f0), .out(out_18), .sel(stop));  // open: en
  Multiplexer #(.width(32)) multiplexer_9 (.in0(in_9), .in1(32'h12508), .out(out_19), .sel(stop));  // open: en
  Multiplexer #(.width(32)) multiplexer_10 (.in0(in_10), .in1(32'hb908), .out(out_20), .sel(stop));  // open: en
  Multiplexer #(.width(32)) multiplexer_11 (.in0({32{1'b0}}), .in1(32'hf0), .out(out_21), .sel(stop));  // open: en
  Multiplexer #(.width(32)) multiplexer_12 (.in0({32{1'b0}}), .in1(32'hfc00), .out(out_22), .sel(stop));  // open: en
  Multiplexer #(.width(32)) multiplexer_13 (.in0({32{1'b0}}), .in1(32'h12008), .out(out_24), .sel(stop));  // open: en
  Multiplexer #(.width(32)) multiplexer_14 (.in0({32{1'b0}}), .in1(32'h121f0), .out(out_23), .sel(stop));  // open: en
  Multiplexer #(.width(32)) multiplexer_15 (.in0({32{1'b0}}), .in1(32'hfdf0), .out(out_26), .sel(stop));  // open: en
  Multiplexer #(.width(32)) multiplexer_16 (.in0({32{1'b0}}), .in1(32'h12008), .out(out_25), .sel(stop));  // open: en
  Multiplexer #(.width(32)) multiplexer_17 (.in0({32{1'b0}}), .in1(32'h1fdf8), .out(out_28), .sel(stop));  // open: en
  Multiplexer #(.width(32)) multiplexer_18 (.in0({32{1'b0}}), .in1({32{1'b0}}), .out(out_27), .sel(stop));  // open: en
  Multiplexer #(.width(32)) multiplexer_19 (.in0({32{1'b0}}), .in1(32'h4148), .out(out_30), .sel(stop));  // open: en
  Multiplexer #(.width(32)) multiplexer_20 (.in0({32{1'b0}}), .in1(32'h8148), .out(out_29), .sel(stop));  // open: en
  Multiplexer #(.width(32)) multiplexer_21 (.in0({32{1'b0}}), .in1(32'h8000), .out(out_31), .sel(stop));  // open: en
  Multiplexer #(.width(32)) multiplexer_22 (.in0({32{1'b0}}), .in1(32'h1fdf8), .out(out_32), .sel(stop));  // open: en
  Multiplexer #(.width(32)) multiplexer_23 (.in0({32{1'b0}}), .in1(32'h120), .out(out_33), .sel(stop));  // open: en
  Multiplexer #(.width(32)) multiplexer_24 (.in0({32{1'b0}}), .in1(32'h1fd30), .out(out_34), .sel(stop));  // open: en
  Multiplexer #(.width(32)) multiplexer_25 (.in0({32{1'b0}}), .in1(32'h12400), .out(out_36), .sel(stop));  // open: en
  Multiplexer #(.width(32)) multiplexer_26 (.in0({32{1'b0}}), .in1(32'h124c8), .out(out_35), .sel(stop));  // open: en
  Multiplexer #(.width(32)) multiplexer_27 (.in0({32{1'b0}}), .in1({32{1'b0}}), .out(out_38), .sel(stop));  // open: en
  Multiplexer #(.width(32)) multiplexer_28 (.in0({32{1'b0}}), .in1(32'h12400), .out(out_37), .sel(stop));  // open: en
  Multiplexer #(.width(32)) multiplexer_29 (.in0({32{1'b0}}), .in1({32{1'b0}}), .out(out_40), .sel(stop));  // open: en
  Multiplexer #(.width(32)) multiplexer_30 (.in0({32{1'b0}}), .in1({32{1'b0}}), .out(out_39), .sel(stop));  // open: en
  Multiplexer #(.width(32)) multiplexer_31 (.in0({32{1'b0}}), .in1({32{1'b0}}), .out(out_42), .sel(stop));  // open: en
  Multiplexer #(.width(32)) multiplexer_32 (.in0({32{1'b0}}), .in1({32{1'b0}}), .out(out_41), .sel(stop));  // open: en

  // Other names for the same wires on the sheet: D1[31:0] = in_2; D2[31:0] = in_3; D3[31:0] = in_4; D4[31:0] = in_5;
  //   D5[31:0] = in_6; D6[31:0] = in_7; D7[31:0] = in_8; D8[31:0] = in_9; D9[31:0] = in_10
endmodule

module dinovis (
);

  DotMatrix #(.matrixcols(32), .matrixrows(20)) dotmatrix_1 (
    .col0(20'h40), .col1(20'h20), .col2(20'h10), .col3(20'h3e), .col4(20'h7a), .col5(20'h3f8),
    .col6(20'h3fe), .col7(20'h2a2), .col8(20'h2b0), .col9({20{1'b0}}));  // open: col10, col11, col12, col13, col14, col15, col16, col17, col18, col19, col20, col21, col22, col23, col24, col25, col26, col27, col28, col29, col30, col31
endmodule

module logic_jump (
  input  [31:0] di_in,
  input  clock,
  input  jmp_btn,
  output [31:0] di_out
);

  wire comparator_1_gt, comparator_1_lt, comparator_2_eq, d_ff_1_q;
  wire [4:0] counter_1_q, multiplexer_1_out;
  wire [31:0] multiplexer_2_out, multiplexer_3_out, multiplexer_4_out, shifter_1_out, shifter_2_out;

  D_Flip_Flop d_ff_1 (
    .clk(clock), .D(jmp_btn), .Q(d_ff_1_q), .preset(d_ff_1_q), .reset(comparator_2_eq));  // open: Qn, en
  Counter #(.width(5), .max('h1f)) counter_1 (
    .count(d_ff_1_q), .Q(counter_1_q), .clk(clock), .clr(comparator_2_eq));  // open: load, D, carry
  Comparator #(.width(5)) comparator_1 (
    .a(counter_1_q), .b(5'b00111), .gt(comparator_1_gt), .lt(comparator_1_lt));  // open: eq
  Shifter #(.width(32), .shift("lr")) shifter_1 (.in(di_out), .\dist (5'b00001), .out(shifter_1_out));
  Shifter #(.width(32)) shifter_2 (.in(di_out), .\dist (multiplexer_1_out), .out(shifter_2_out));
  Multiplexer #(.width(5)) multiplexer_1 (
    .in0({5{1'b0}}), .in1(5'b00001), .out(multiplexer_1_out), .sel(comparator_1_lt));  // open: en
  Multiplexer #(.width(32)) multiplexer_2 (
    .in0(di_in), .in1(shifter_1_out), .out(multiplexer_2_out), .sel(comparator_1_gt));  // open: en
  Multiplexer #(.width(32)) multiplexer_3 (
    .in0(di_in), .in1(shifter_2_out), .out(multiplexer_3_out), .sel(d_ff_1_q));  // open: en
  Register #(.width(32)) register_1 (.D(multiplexer_4_out), .Q(di_out), .clk(clock));  // open: en, clr
  Comparator #(.width(5)) comparator_2 (.a(counter_1_q), .b(5'b10000), .eq(comparator_2_eq));  // open: gt, lt
  Multiplexer #(.width(32)) multiplexer_4 (
    .in0(multiplexer_3_out), .in1(multiplexer_2_out), .out(multiplexer_4_out), .sel(comparator_1_gt));  // open: en
endmodule

module jump (
  input  clock,
  input  jump,
  output [31:0] out_3,
  output [31:0] out_4,
  output [31:0] out_5,
  output [31:0] out_6,
  output [31:0] out_7,
  output [31:0] out_8,
  output [31:0] out_9,
  output [31:0] out_10,
  output [31:0] out_11
);

  wire comparator_1_eq;
  wire [5:0] counter_1_q;

  Counter #(.width(6), .max('h20)) counter_1 (
    .Q(counter_1_q), .clk(clock), .clr(comparator_1_eq));  // open: load, D, count, carry
  Comparator #(.width(6)) comparator_1 (.a(counter_1_q), .b(6'b100000), .eq(comparator_1_eq));  // open: gt, lt
  logic_jump logic_jump_1 (.di_in(32'h40), .clock(comparator_1_eq), .jmp_btn(jump), .di_out(out_3));
  logic_jump logic_jump_2 (.di_in(32'h20), .clock(comparator_1_eq), .jmp_btn(jump), .di_out(out_4));
  logic_jump logic_jump_3 (.di_in(32'h10), .clock(comparator_1_eq), .jmp_btn(jump), .di_out(out_5));
  logic_jump logic_jump_4 (.di_in(32'h3f8), .clock(comparator_1_eq), .jmp_btn(jump), .di_out(out_8));
  logic_jump logic_jump_5 (.di_in(32'h3e), .clock(comparator_1_eq), .jmp_btn(jump), .di_out(out_6));
  logic_jump logic_jump_6 (.di_in(32'h7a), .clock(comparator_1_eq), .jmp_btn(jump), .di_out(out_7));
  logic_jump logic_jump_7 (.di_in(32'h3fe), .clock(comparator_1_eq), .jmp_btn(jump), .di_out(out_9));
  logic_jump logic_jump_8 (.di_in(32'h2a2), .clock(comparator_1_eq), .jmp_btn(jump), .di_out(out_10));
  logic_jump logic_jump_9 (.di_in(32'h2b0), .clock(comparator_1_eq), .jmp_btn(jump), .di_out(out_11));
endmodule
